// Logisim project ALU (2).circ as structural Verilog: 11 circuits, main circuit onebitHalfAdder
module main (
  input  B3,
  input  B2,
  input  B1,
  input  B0,
  input  A3,
  input  A2,
  input  A1,
  input  A0,
  input  AInvert,
  input  BInvert,
  input  ALU_Operation,
  input  in_12,
  output Sign,
  output Zero,
  output Overflow,
  output R3,
  output R2,
  output R1,
  output R0
);

  wire and_1_out, clock_1_out, fourbitreg_2_q0, fourbitreg_2_q1, fourbitreg_2_q2, fourbitreg_2_q3,
       fourbitreg_3_q0, fourbitreg_3_q1, fourbitreg_3_q2, fourbitreg_3_q3, not_1_out, not_2_out, not_3_out,
       not_4_out, onebitalu_1_carryout, onebitalu_1_result, onebitalu_2_carryout, onebitalu_2_result,
       onebitalu_3_carryout, onebitalu_3_result, onebitalu_4_carryout, onebitalu_4_result, onebitreg_1_q0,
       onebitreg_2_q0, overflowdectection_1_overflow, twobitreg_1_q0, twobitreg_1_q1;

  Clock clock_1 (.out(clock_1_out));
  oneBitReg onebitreg_1 (.Clock(clock_1_out), .D0(AInvert), .Q0(onebitreg_1_q0));
  oneBitReg onebitreg_2 (.Clock(clock_1_out), .D0(BInvert), .Q0(onebitreg_2_q0));
  twoBitReg twobitreg_1 (.Clock(clock_1_out), .D1(ALU_Operation), .D0(in_12), .Q1(twobitreg_1_q1), .Q0(twobitreg_1_q0));
  oneBitALU onebitalu_1 (
    .A(fourbitreg_3_q3), .CarryIn(onebitalu_2_carryout), .B(fourbitreg_2_q3), .BInvert(onebitreg_2_q0),
    .in_3(onebitreg_1_q0), .in_4(twobitreg_1_q1), .in_2(twobitreg_1_q0), .Result(onebitalu_1_result),
    .CarryOut(onebitalu_1_carryout));
  fourBitReg fourbitreg_1 (
    .Clock(clock_1_out), .D3(onebitalu_1_result), .D2(onebitalu_2_result), .D1(onebitalu_3_result),
    .D0(onebitalu_4_result), .Q3(R3), .Q2(R2), .Q1(R1), .Q0(R0));
  fourBitReg fourbitreg_2 (
    .Clock(clock_1_out), .D3(B3), .D2(B2), .D1(B1), .D0(B0), .Q3(fourbitreg_2_q3), .Q2(fourbitreg_2_q2),
    .Q1(fourbitreg_2_q1), .Q0(fourbitreg_2_q0));
  not not_1 (not_1_out, onebitalu_1_result);
  oneBitALU onebitalu_2 (
    .A(fourbitreg_3_q2), .CarryIn(onebitalu_3_carryout), .B(fourbitreg_2_q2), .BInvert(onebitreg_2_q0),
    .in_3(onebitreg_1_q0), .in_4(twobitreg_1_q1), .in_2(twobitreg_1_q0), .Result(onebitalu_2_result),
    .CarryOut(onebitalu_2_carryout));
  not not_2 (not_2_out, onebitalu_2_result);
  oneBitALU onebitalu_3 (
    .A(fourbitreg_3_q1), .CarryIn(onebitalu_4_carryout), .B(fourbitreg_2_q1), .BInvert(onebitreg_2_q0),
    .in_3(onebitreg_1_q0), .in_4(twobitreg_1_q1), .in_2(twobitreg_1_q0), .Result(onebitalu_3_result),
    .CarryOut(onebitalu_3_carryout));
  fourBitReg fourbitreg_3 (
    .Clock(clock_1_out), .D3(A3), .D2(A2), .D1(A1), .D0(A0), .Q3(fourbitreg_3_q3), .Q2(fourbitreg_3_q2),
    .Q1(fourbitreg_3_q1), .Q0(fourbitreg_3_q0));
  not not_3 (not_3_out, onebitalu_3_result);
  not not_4 (not_4_out, onebitalu_4_result);
  oneBitALU onebitalu_4 (
    .A(fourbitreg_3_q0), .CarryIn(onebitreg_2_q0), .B(fourbitreg_2_q0), .BInvert(onebitreg_2_q0),
    .in_3(onebitreg_1_q0), .in_4(twobitreg_1_q1), .in_2(twobitreg_1_q0), .Result(onebitalu_4_result),
    .CarryOut(onebitalu_4_carryout));
  and and_1 (and_1_out, not_1_out, not_2_out, not_3_out, not_4_out);
  overflowDectection overflowdectection_1 (
    .SignBitA(fourbitreg_3_q3), .SignBitB(fourbitreg_2_q3), .ResultSignBit(onebitalu_1_result),
    .CarryOut(onebitalu_1_carryout), .Overflow(overflowdectection_1_overflow));
  threeBitReg threebitreg_1 (
    .Clock(clock_1_out), .D2(onebitalu_1_result), .D1(and_1_out), .D0(overflowdectection_1_overflow),
    .Q2(Sign), .Q1(Zero), .Q0(Overflow));

  // Notes on the sheet:
  //   Jingwen Xiao, 260885501
  //   B
  //   Result
  //   A
  //   Status output
endmodule

module onebitHalfAdder (
  input  in_1,
  input  A,
  output out_3,
  output out_4
);

  wire and_2_out, and_3_out, not_1_out, not_2_out;

  not not_1 (not_1_out, in_1);
  not not_2 (not_2_out, A);
  and and_1 (out_4, A, in_1);
  and and_2 (and_2_out, not_1_out, A);
  and and_3 (and_3_out, not_2_out, in_1);
  or or_1 (out_3, and_2_out, and_3_out);

  // Notes on the sheet:
  //   B
endmodule

module oneBitFullAdder (
  input  C,
  input  A,
  input  B,
  output SUM,
  output Carryout
);

  wire onebithalfadder_1_out_3, onebithalfadder_1_out_4, onebithalfadder_2_out_4;

  onebitHalfAdder onebithalfadder_1 (.in_1(A), .A(B), .out_3(onebithalfadder_1_out_3), .out_4(onebithalfadder_1_out_4));
  onebitHalfAdder onebithalfadder_2 (
    .in_1(C), .A(onebithalfadder_1_out_3), .out_3(SUM), .out_4(onebithalfadder_2_out_4));
  or or_1 (Carryout, onebithalfadder_2_out_4, onebithalfadder_1_out_4);
endmodule

module oneBitMux (
  input  A,
  input  B,
  input  Select,
  output C
);

  wire and_1_out, and_2_out, not_1_out;

  not not_1 (not_1_out, Select);
  and and_1 (and_1_out, A, not_1_out);
  and and_2 (and_2_out, Select, B);
  or or_1 (C, and_1_out, and_2_out);
endmodule

module twoBitMux (
  input  _0,
  input  _1,
  input  _2,
  input  _3,
  input  in_5,
  input  in_6,
  output out_7
);

  wire and_1_out, and_2_out, and_3_out, and_4_out, not_1_out, not_2_out;

  not not_1 (not_1_out, in_5);
  not not_2 (not_2_out, in_6);
  and and_1 (and_1_out, _0, not_1_out, not_2_out);
  and and_2 (and_2_out, _1, not_1_out, in_6);
  and and_3 (and_3_out, _2, not_2_out, in_5);
  and and_4 (and_4_out, _3, in_5, in_6);
  or or_1 (out_7, and_1_out, and_2_out, and_3_out, and_4_out);

  // Notes on the sheet:
  //   s0
  //   s1
endmodule

module oneBitALU (
  input  A,
  input  in_2,
  input  in_3,
  input  in_4,
  input  CarryIn,
  input  B,
  input  BInvert,
  output Result,
  output CarryOut
);

  wire and_1_out, not_1_out, not_2_out, onebitfulladder_1_sum, or_1_out, PA, PB;

  not not_1 (not_1_out, A);
  not not_2 (not_2_out, B);
  oneBitMux onebitmux_1 (.A(A), .B(not_1_out), .Select(in_3), .C(PA));
  oneBitMux onebitmux_2 (.A(B), .B(not_2_out), .Select(BInvert), .C(PB));
  and and_1 (and_1_out, PA, PB);
  or or_1 (or_1_out, PA, PB);
  twoBitMux twobitmux_1 (
    ._0(and_1_out), ._1(or_1_out), ._2(onebitfulladder_1_sum), .in_5(in_4), .in_6(in_2), .out_7(Result));  // open: _3
  oneBitFullAdder onebitfulladder_1 (.C(CarryIn), .A(PA), .B(PB), .SUM(onebitfulladder_1_sum), .Carryout(CarryOut));

  // Notes on the sheet:
  //   AInvert
endmodule

module oneBitReg (
  input  Clock,
  input  D0,
  output Q0
);

  D_Flip_Flop d_ff_1 (.clk(Clock), .D(D0), .Q(Q0));  // open: Qn, preset, reset

  // Notes on the sheet:
  //   D0
  //   Q0
endmodule

module twoBitReg (
  input  Clock,
  input  D1,
  input  D0,
  output Q1,
  output Q0
);

  D_Flip_Flop d_ff_1 (.D(D1), .clk(Clock), .Q(Q1));  // open: Qn, preset, reset
  D_Flip_Flop d_ff_2 (.D(D0), .clk(Clock), .Q(Q0));  // open: Qn, preset, reset

  // Notes on the sheet:
  //   Clock
  //   D1
  //   Q1
  //   D0
  //   Q0
endmodule

module fourBitReg (
  input  Clock,
  input  D3,
  input  D2,
  input  D1,
  input  D0,
  output Q3,
  output Q2,
  output Q1,
  output Q0
);

  D_Flip_Flop d_ff_1 (.D(D3), .clk(Clock), .Q(Q3));  // open: Qn, preset, reset
  D_Flip_Flop d_ff_2 (.D(D2), .clk(Clock), .Q(Q2));  // open: Qn, preset, reset
  D_Flip_Flop d_ff_3 (.D(D1), .clk(Clock), .Q(Q1));  // open: Qn, preset, reset
  D_Flip_Flop d_ff_4 (.D(D0), .clk(Clock), .Q(Q0));  // open: Qn, preset, reset

  // Notes on the sheet:
  //   Clock
  //   D3
  //   Q3
  //   D2
  //   Q2
  //   D1
  //   Q1
  //   D0
  //   Q0
endmodule

module threeBitReg (
  input  Clock,
  input  D2,
  input  D1,
  input  D0,
  output Q2,
  output Q1,
  output Q0
);

  D_Flip_Flop d_ff_1 (.D(D2), .clk(Clock), .Q(Q2));  // open: Qn, preset, reset
  D_Flip_Flop d_ff_2 (.D(D1), .clk(Clock), .Q(Q1));  // open: Qn, preset, reset
  D_Flip_Flop d_ff_3 (.D(D0), .clk(Clock), .Q(Q0));  // open: Qn, preset, reset
endmodule

module overflowDectection (
  input  SignBitA,
  input  SignBitB,
  input  ResultSignBit,
  input  CarryOut,
  output Overflow
);

  wire and_1_out, not_1_out, xor_1_out, xor_2_out;

  xor xor_1 (xor_1_out, SignBitA, SignBitB);
  not not_1 (not_1_out, xor_1_out);
  xor xor_2 (xor_2_out, SignBitB, ResultSignBit);
  and and_1 (and_1_out, not_1_out, xor_2_out);
  or or_1 (Overflow, and_1_out, CarryOut);

  // Notes on the sheet:
  //   Result Sign Differs from Input Sign Check
  //   UnSignedOverFlowCheck
  //   Similar Sign Check
  //   If Both Conditions are true (I.e., inputs have similar sign and the result sign differes, then Sign overflow happens)
endmodule
