// Logisim project KITT.circ as structural Verilog: 1 circuit, main circuit KITT
module KITT (
);

  wire clock_1_out, d_ff_1_q, d_ff_2_q, d_ff_3_q, d_ff_4_q, d_ff_5_q, d_ff_6_q, d_ff_7_q, d_ff_8_q, d_ff_9_q,
       d_ff_10_q, d_ff_11_q, d_ff_12_q, d_ff_13_q, d_ff_14_q, not_1_out, or_1_out, or_2_out, or_3_out,
       or_4_out, or_5_out, or_6_out, or_7_out, or_8_out;

  Clock clock_1 (.out(clock_1_out));
  or or_1 (or_1_out, not_1_out, d_ff_3_q);
  D_Flip_Flop d_ff_1 (.D(or_1_out), .clk(clock_1_out), .Q(d_ff_1_q));  // open: Qn, preset, reset
  D_Flip_Flop d_ff_2 (.D(d_ff_1_q), .clk(clock_1_out), .Q(d_ff_2_q));  // open: Qn, preset, reset
  D_Flip_Flop d_ff_3 (.D(d_ff_5_q), .clk(clock_1_out), .Q(d_ff_3_q));  // open: Qn, preset, reset
  or or_2 (or_2_out, d_ff_3_q, d_ff_2_q);
  D_Flip_Flop d_ff_4 (.D(d_ff_2_q), .clk(clock_1_out), .Q(d_ff_4_q));  // open: Qn, preset, reset
  D_Flip_Flop d_ff_5 (.D(d_ff_7_q), .clk(clock_1_out), .Q(d_ff_5_q));  // open: Qn, preset, reset
  not not_1 (not_1_out, or_4_out);
  LED led_1 (.in(d_ff_1_q));
  LED led_2 (.in(or_2_out));
  or or_3 (or_3_out, d_ff_4_q, d_ff_5_q);
  D_Flip_Flop d_ff_6 (.D(d_ff_4_q), .clk(clock_1_out), .Q(d_ff_6_q));  // open: Qn, preset, reset
  D_Flip_Flop d_ff_7 (.D(d_ff_9_q), .clk(clock_1_out), .Q(d_ff_7_q));  // open: Qn, preset, reset
  or or_4 (or_4_out, d_ff_1_q, or_2_out, or_3_out, or_5_out, or_6_out, or_7_out, or_8_out, d_ff_14_q);
  LED led_3 (.in(or_3_out));
  LED led_4 (.in(or_5_out));
  LED led_5 (.in(or_6_out));
  or or_5 (or_5_out, d_ff_6_q, d_ff_7_q);
  D_Flip_Flop d_ff_8 (.D(d_ff_6_q), .clk(clock_1_out), .Q(d_ff_8_q));  // open: Qn, preset, reset
  D_Flip_Flop d_ff_9 (.D(d_ff_11_q), .clk(clock_1_out), .Q(d_ff_9_q));  // open: Qn, preset, reset
  LED led_6 (.in(or_7_out));
  LED led_7 (.in(or_8_out));
  or or_6 (or_6_out, d_ff_8_q, d_ff_9_q);
  LED led_8 (.in(d_ff_14_q));
  or or_7 (or_7_out, d_ff_10_q, d_ff_11_q);
  D_Flip_Flop d_ff_10 (.D(d_ff_8_q), .clk(clock_1_out), .Q(d_ff_10_q));  // open: Qn, preset, reset
  D_Flip_Flop d_ff_11 (.D(d_ff_13_q), .clk(clock_1_out), .Q(d_ff_11_q));  // open: Qn, preset, reset
  D_Flip_Flop d_ff_12 (.D(d_ff_10_q), .clk(clock_1_out), .Q(d_ff_12_q));  // open: Qn, preset, reset
  D_Flip_Flop d_ff_13 (.D(d_ff_14_q), .clk(clock_1_out), .Q(d_ff_13_q));  // open: Qn, preset, reset
  or or_8 (or_8_out, d_ff_12_q, d_ff_13_q);
  D_Flip_Flop d_ff_14 (.D(d_ff_12_q), .clk(clock_1_out), .Q(d_ff_14_q));  // open: Qn, preset, reset

  // Notes on the sheet:
  //   Jingwen Xiao, 260885501
endmodule
