// Logisim project SequentialDivider (2).circ as structural Verilog: 1 circuit, main circuit main
module main (
  input  [3:0] Divisor,
  input  [3:0] Dividend,
  input  RESET,
  output [3:0] Quotient,
  output DONE,
  output [7:0] Remainder
);

  wire and_1_out, clock_1_out, not_1_out, not_2_out, not_3_out, not_4_out, subtractor_1_bout;
  wire [7:0] bit_extender_1_out, multiplexer_1_out, shift_register_1_out, subtractor_1_out;

  assign bit_extender_1_out = {{4{1'b0}}, Dividend};  // Bit_Extender bit_extender_1
  not not_1 (not_1_out, RESET);
  Shift_Register shift_register_1 (
    .shift(not_1_out), .in(1'b0), .clk(clock_1_out), .out(shift_register_1_out[0]), .load(RESET),
    .d0(Divisor[3]), .q0(shift_register_1_out[7]), .d1(Divisor[2]), .q1(shift_register_1_out[6]),
    .d2(Divisor[1]), .q2(shift_register_1_out[5]), .d3(Divisor[0]), .q3(shift_register_1_out[4]), .d4(1'b0),
    .q4(shift_register_1_out[3]), .d5(1'b0), .q5(shift_register_1_out[2]), .d6(1'b0),
    .q6(shift_register_1_out[1]), .d7(1'b0));  // open: clr, q7
  Subtractor subtractor_1 (
    .a(Remainder), .b(shift_register_1_out), .out(subtractor_1_out), .bin(1'b0), .bout(subtractor_1_bout));
  not not_2 (not_2_out, subtractor_1_bout);
  Multiplexer #(.width(8)) multiplexer_1 (
    .in0(subtractor_1_out), .in1(bit_extender_1_out), .out(multiplexer_1_out), .sel(RESET));
  Register register_1 (.D(multiplexer_1_out), .en(and_1_out), .Q(Remainder), .clk(clock_1_out));  // open: clr
  and and_1 (and_1_out, not_2_out, not_4_out);
  Shift_Register shift_register_2 (
    .shift(not_4_out), .in(not_3_out), .clk(clock_1_out), .clr(RESET), .q0(Quotient[0]), .q1(Quotient[1]),
    .q2(Quotient[2]), .q3(Quotient[3]));  // open: out, load, d0, d1, d2, d3, d4, q4, d5, q5, d6, q6, d7, q7
  not not_3 (not_3_out, subtractor_1_bout);
  Clock clock_1 (.out(clock_1_out));
  Counter #(.max('h5), .ongoal("stay")) counter_1 (
    .carry(DONE), .clk(clock_1_out), .clr(RESET));  // open: load, D, count, Q, up
  not not_4 (not_4_out, DONE);

  // Other names for the same wires on the sheet: Initalize = RESET

  // Notes on the sheet:
  //   Jingwen Xiao,260885501
endmodule
